# Fritzing sketch sketch_sequencer (saved by Fritzing 1.0.5)

parts:
  IC1 = TL074 Quad Opamp (Movable) [package="DIP (Dual Inline)"]
  IC1_PWR = TL074 Quad Opamp (Movable) [package="DIP (Dual Inline)"]  # not connected
  IC1_A = TL074 Quad Opamp (Movable) [package="DIP (Dual Inline)"]  # not connected
  IC1_B = TL074 Quad Opamp (Movable) [package="DIP (Dual Inline)"]  # not connected
  IC1_C = TL074 Quad Opamp (Movable) [package="DIP (Dual Inline)"]  # not connected
  IC1_D = TL074 Quad Opamp (Movable) [package="DIP (Dual Inline)"]  # not connected
  J1 = shrouded pin header, 16 pins [form="♂ (shrouded male)"]
  MH-ET_Live_Minikit_for_ESP1 = MH-ET Live Minikit for ESP32
  VR1 = Trimpot-#3296-flat [power=0.5W knob_status=50% maximum_resistance=10kΩ part_number=1k package=3386u]
  R1 = Resistor [tolerance=±5% resistance=6k package="0603 [SMD]"]
  R2 = Resistor [tolerance=±5% resistance=10k package="0603 [SMD]"]
  C1 = Tantalum Capacitor [capacitance=100nF voltage=35V package="D 7343 [SMD, tantalum]"]
  TRRS1 = Audio Jack (TRRS) 3.5mm [part_number="LUMBERG JEITA RC-5325A" package="RC-5325A [SMD]"]

nets (from the breadboard view):
  N1: IC1.connector0, R1.Pin_0, C1.-, TRRS1.TIP
  N2: IC1.connector1, VR1.WIPER, R2.Pin_0
  N3: IC1.connector2, MH-ET_Live_Minikit_for_ESP1.IO25
  N4: IC1.connector3, J1.pin12
  N5: IC1.connector4, IC1.connector9, J1.pin14, R2.Pin_1
  N6: IC1.connector5, IC1.connector6
  N7: IC1.connector7, IC1.connector8
  N8: IC1.connector10, J1.pin16
  N9: IC1.connector11, J1.pin13, MH-ET_Live_Minikit_for_ESP1.GND
  N10: IC1.connector12, IC1.connector13
  N11: J1.pin4, TRRS1.SLEEVE
  N12: J1.pin6, MH-ET_Live_Minikit_for_ESP1.VCC
  N13: J1.pin15, C1.+
  N14: VR1.CCW, R1.Pin_1

custom parts:
  TL074 Quad Opamp (Movable): Quadruple Operational Amplifier (Opamp)
  TL074 Quad Opamp (Movable): Quadruple Operational Amplifier (Opamp)
  TL074 Quad Opamp (Movable): Quadruple Operational Amplifier (Opamp)
  TL074 Quad Opamp (Movable): Quadruple Operational Amplifier (Opamp)
  TL074 Quad Opamp (Movable): Quadruple Operational Amplifier (Opamp)
  TL074 Quad Opamp (Movable): Quadruple Operational Amplifier (Opamp)
  MH-ET Live Minikit for ESP32: MH-ET Live Minikit for ESP32 ( http://mh.nodebb.com/topic/8/mh-et-live-minikit-for-esp32/2/) PCB footprint is invalid.
  Trimpot-#3296-flat: Bourns #3296 Square Trimpot 25 turn lying flat for low profile
